# Fritzing sketch Conexao_bmp680 (saved by Fritzing 0.9.3b)

parts:
  Componente1 = HUZZAH ESP8266 Breakout
  Componente2 = Adafruit BME680 [part_number="Adafruit #3660"]

nets:
  GND: Componente1.GND, Componente2.GND
  3.3V: Componente1.3.3V, Componente2.3.3V
  N1: Componente1.GPIO4, Componente2.SDI/SDA
  N2: Componente1.GPIO5, Componente2.SCK/SCL

custom parts:
  HUZZAH ESP8266 Breakout: The ESP8266 processor from Espressif is an 80 MHz microcontroller with a full WiFi front-end (both as client and access point) and TCP/IP stack with DNS support as well.
