# Fritzing sketch Conexao_pms (saved by Fritzing 0.9.3b)

parts:
  Componente1 = HUZZAH ESP8266 Breakout
  Componente2 = Arduino Uno (Rev3)
  J1 = female pin header, 2 pins [form="♀ (female)"]
  J2 = female pin header, 2 pins [form="♀ (female)"]
  J3 = female pin header, 2 pins [form="♀ (female)"]
  J4 = female pin header, 2 pins [form="♀ (female)"]

nets:
  N1: Componente1.RXD_5V, J4.pin2
  N2: Componente1.TXD, J3.pin2
  N3: Componente2.GND, J1.pin1
  N4: Componente2.D0/RX, J3.pin1
  N5: Componente2.D1/TX, J4.pin1
  N6: Componente2.D2, J2.pin2
  N7: Componente2.D3_PWM, J2.pin1
  N8: Componente2.5V, J1.pin2

notes:
  Conversor lógico
  PMS

custom parts:
  HUZZAH ESP8266 Breakout: The ESP8266 processor from Espressif is an 80 MHz microcontroller with a full WiFi front-end (both as client and access point) and TCP/IP stack with DNS support as well.
