# Fritzing sketch Esquemático_arduino (saved by Fritzing 0.9.3b)

parts:
  Componente1 = Arduino Mega ADK (Rev3)
  3_3V1 = Battery Holders [package=lipo-1100mAh]
  BMP281 = Adafruit_BMP280
  Clock1 = Real Time Clock Module - DS1307 RTC Breakout Board
  SdCard1 = MicroSD Card Module
  VCC_PMS1 = female pin header, 2 pins [form="♀ (female)"]
  RXTXPMS1 = female pin header, 2 pins [form="♀ (female)"]  # not connected

nets:
  N1: Componente1.D21/SCL, BMP281.SCK/SCL, Clock1.SCL
  N2: Componente1.D20/SDA, BMP281.SDI/SDA, Clock1.SDA
  N3: Componente1.D19/RX1, VCC_PMS1.pin1
  N4: Componente1.D18/TX1, VCC_PMS1.pin2
  N5: Componente1.D50/MISO, SdCard1.MISO
  N6: Componente1.D51/MOSI, SdCard1.MOSI
  N7: Componente1.D52/SCK, SdCard1.SCK
  N8: Componente1.D53/SS, SdCard1.CS
  N9: 3_3V1.+, Clock1.5V

custom parts:
  Adafruit_BMP280: Bosch has stepped up their game with their new BMP280 sensor, an environmental sensor with temperature, barometric pressure that is the next generation upgrade to the BMP085/BMP180/BMP183. This sensor is great for all sorts of weather sensing and can even be used in both I2C and SPI! This precision sensor from Bosch is the best low-cost, precision sensing solution for measuring barometric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
